// Logisim project schematic.circ as structural Verilog: 1 circuit, main circuit main
module main (
  input  clk,
  input  start,
  input  [31:0] dividend,
  input  [31:0] divisor,
  output [31:0] remainder,
  output [31:0] quotient,
  output done
);

  wire comparator_1_eq, not_1_out, not_2_out;
  wire [0:0] comparator_2_lt;
  wire [31:0] b_q, counter_q, multiplexer_1_out, multiplexer_2_out, multiplexer_3_out, multiplexer_4_out,
       multiplexer_5_out, subtractor_1_out, subtractor_2_out;
  wire [63:0] shifter_1_out;

  Multiplexer #(.select(2), .width(32)) multiplexer_1 (
    .in0(shifter_1_out[63:32]), .in1(shifter_1_out[63:32]), .in2(subtractor_2_out), .in3(remainder),
    .out(multiplexer_1_out), .sel({counter_q[0], comparator_2_lt[0]}));
  Multiplexer #(.select(2), .width(32)) multiplexer_2 (
    .in0(shifter_1_out[31:0]), .in1(shifter_1_out[31:0]), .in2({quotient[31:1], 1'b1}), .in3(quotient),
    .out(multiplexer_2_out), .sel({counter_q[0], comparator_2_lt[0]}));
  Multiplexer #(.width(32)) multiplexer_3 (
    .in0(multiplexer_1_out), .in1({32{1'b0}}), .out(multiplexer_3_out), .sel(start));
  Multiplexer #(.width(32)) multiplexer_4 (
    .in0(multiplexer_2_out), .in1(dividend), .out(multiplexer_4_out), .sel(start));
  Multiplexer #(.width(32)) multiplexer_5 (.in0(subtractor_1_out), .in1(32'h40), .out(multiplexer_5_out), .sel(start));
  Register #(.width(32)) a (.D(multiplexer_3_out), .en(not_1_out), .clk(clk), .Q(remainder));  // open: clr
  Register #(.width(32)) b (.D(divisor), .en(start), .clk(clk), .Q(b_q));  // open: clr
  Register #(.width(32)) q (.D(multiplexer_4_out), .en(not_1_out), .clk(clk), .Q(quotient));  // open: clr
  Register #(.width(32)) counter (.D(multiplexer_5_out), .en(not_1_out), .clk(clk), .Q(counter_q));  // open: clr
  Subtractor #(.width(32)) subtractor_1 (.a(counter_q), .b(32'h1), .out(subtractor_1_out));  // open: bin, bout
  Shifter #(.width(64)) shifter_1 (.in({remainder, quotient}), .\dist (6'b000001), .out(shifter_1_out));
  Comparator #(.width(32)) comparator_1 (.a(counter_q), .b({32{1'b0}}), .eq(comparator_1_eq));  // open: gt, lt
  not not_1 (not_1_out, done);
  Comparator #(.width(32)) comparator_2 (.a(remainder), .b(b_q), .lt(comparator_2_lt[0]));  // open: gt, eq
  not not_2 (not_2_out, start);
  Subtractor #(.width(32)) subtractor_2 (.a(remainder), .b(b_q), .out(subtractor_2_out));  // open: bin, bout
  and and_1 (done, comparator_1_eq, not_2_out);
endmodule
